// Logisim project cpu.circ as structural Verilog: 4 circuits, main circuit main
module main (
);

  wire _0_out, _1_out, _2_out, _3_out, _4_out, _5_out, _6_out, _7_out, C_out, Clock_out;
  wire [7:0] cpu_1_memory_address, cpu_1_output, ram_1_data, t_ff_1_q;

  RAM ram_1 (.addr(cpu_1_memory_address), .data(ram_1_data));  // open: sel, clk, ld, clr
  CPU cpu_1 (
    .Memory_In(ram_1_data), .Input(t_ff_1_q), .Memory_Address(cpu_1_memory_address), .Output(cpu_1_output),
    .Clock(Clock_out));
  Clock Clock (.out(Clock_out));
  Hex_Digit_Display hex_digit_display_1 (.value(cpu_1_output[7:4]));  // open: dp
  Hex_Digit_Display hex_digit_display_2 (.value(t_ff_1_q[7:4]));  // open: dp
  Hex_Digit_Display hex_digit_display_3 (.value(cpu_1_output[3:0]));  // open: dp
  Hex_Digit_Display hex_digit_display_4 (.value(t_ff_1_q[3:0]));  // open: dp
  Button _0 (.out(_0_out));
  Button _1 (.out(_1_out));
  Button _2 (.out(_2_out));
  Button _3 (.out(_3_out));
  Button _4 (.out(_4_out));
  Button _5 (.out(_5_out));
  Button _6 (.out(_6_out));
  Button _7 (.out(_7_out));
  Button C (.out(C_out));
  T_Flip_Flop t_ff_1 (.clk(_0_out), .T(_0_out), .Q(t_ff_1_q[0]), .reset(C_out));  // open: Qn, preset, en
  T_Flip_Flop t_ff_2 (.clk(_1_out), .T(_1_out), .Q(t_ff_1_q[1]), .reset(C_out));  // open: Qn, preset, en
  T_Flip_Flop t_ff_3 (.clk(_2_out), .T(_2_out), .Q(t_ff_1_q[2]), .reset(C_out));  // open: Qn, preset, en
  T_Flip_Flop t_ff_4 (.clk(_3_out), .T(_3_out), .Q(t_ff_1_q[3]), .reset(C_out));  // open: Qn, preset, en
  T_Flip_Flop t_ff_5 (.clk(_4_out), .T(_4_out), .Q(t_ff_1_q[4]), .reset(C_out));  // open: Qn, preset, en
  T_Flip_Flop t_ff_6 (.clk(_5_out), .T(_5_out), .Q(t_ff_1_q[5]), .reset(C_out));  // open: Qn, preset, en
  T_Flip_Flop t_ff_7 (.clk(_6_out), .T(_6_out), .Q(t_ff_1_q[6]), .reset(C_out));  // open: Qn, preset, en
  T_Flip_Flop t_ff_8 (.clk(_7_out), .T(_7_out), .Q(t_ff_1_q[7]), .reset(C_out));  // open: Qn, preset, en
endmodule

module Data_Path (
  input  Clock,
  input  Write_PC,
  input  [7:0] MBR_In,
  input  Write_MBR,
  input  Write_OUT,
  input  [7:0] Switch_Input,
  input  Write_B,
  input  Write_A,
  input  [1:0] B_Bus_Select,
  input  [2:0] F,
  output [7:0] PC_Out,
  output [7:0] MBR_Out,
  output [7:0] OUT_Out
);

  wire [7:0] A_q, alu_1_c, B_q, multiplexer_1_out;

  Register PC (.D(alu_1_c), .en(Write_PC), .Q(PC_Out), .clk(Clock));  // open: clr
  Register OUT (.D(alu_1_c), .en(Write_OUT), .Q(OUT_Out), .clk(Clock));  // open: clr
  Register B (.D(alu_1_c), .en(Write_B), .Q(B_q), .clk(Clock));  // open: clr
  Register A (.D(alu_1_c), .en(Write_A), .Q(A_q), .clk(Clock));  // open: clr
  Register MBR (.D(MBR_In), .en(Write_MBR), .Q(MBR_Out), .clk(Clock));  // open: clr
  Multiplexer #(.select(2), .width(8), .disabled(0), .enable("false")) multiplexer_1 (
    .in0(B_q), .in1(MBR_Out), .in2(PC_Out), .in3(Switch_Input), .out(multiplexer_1_out), .sel(B_Bus_Select));
  ALU alu_1 (.A(A_q), .B(multiplexer_1_out), .F(F), .C(alu_1_c));

  // Notes on the sheet:
  //   A Bus
  //   C Bus
  //   B Bus
endmodule

module ALU (
  input  [7:0] A,
  input  [7:0] B,
  input  [2:0] F,
  output [7:0] C
);

  wire [7:0] adder_1_out, adder_2_out, adder_3_out, and_1_out, or_1_out, subtractor_1_out;

  Hex_Digit_Display hex_digit_display_1 (.value(A[7:4]));  // open: dp
  Hex_Digit_Display hex_digit_display_2 (.value(B[7:4]));  // open: dp
  Hex_Digit_Display hex_digit_display_3 (.value(A[3:0]));  // open: dp
  Hex_Digit_Display hex_digit_display_4 (.value(B[3:0]));  // open: dp
  Adder adder_1 (.a(A), .b(8'h1), .out(adder_1_out));  // open: cin, cout
  Adder adder_2 (.a(B), .b(8'h1), .out(adder_2_out));  // open: cin, cout
  Adder adder_3 (.a(A), .b(B), .out(adder_3_out));  // open: cin, cout
  Subtractor subtractor_1 (.a(A), .b(B), .out(subtractor_1_out));  // open: bin, bout
  assign and_1_out = A & B;  // AND_Gate and_1, 8 bits wide
  assign or_1_out = A | B;  // OR_Gate or_1, 8 bits wide
  Multiplexer #(.select(3), .width(8), .disabled(0), .enable("false")) multiplexer_1 (
    .in0(A), .in1(B), .in2(adder_1_out), .in3(adder_2_out), .in4(adder_3_out), .in5(subtractor_1_out),
    .in6(and_1_out), .in7(or_1_out), .out(C), .sel(F));
  Hex_Digit_Display hex_digit_display_5 (.value(C[7:4]));  // open: dp
  Hex_Digit_Display hex_digit_display_6 (.value(C[3:0]));  // open: dp
endmodule

module CPU (
  input  [7:0] Memory_In,
  input  [7:0] Input,
  input  Clock,
  output [7:0] Memory_Address,
  output [7:0] Output
);

  wire [4:0] data_path_1_mbr_out, multiplexer_1_out;
  wire [7:5] data_path_1_mbr_out_2;
  wire [15:0] MIR_q, rom_1_data;

  Multiplexer #(.width(5), .disabled(0), .enable("false")) multiplexer_1 (
    .in0(MIR_q[15:11]), .in1(data_path_1_mbr_out), .out(multiplexer_1_out), .sel(MIR_q[10]));
  ROM #(.addrWidth(5), .dataWidth(16)) rom_1 (.addr(multiplexer_1_out), .data(rom_1_data));  // open: sel
  Register #(.width(16), .trigger("falling")) MIR (.D(rom_1_data), .Q(MIR_q), .clk(Clock));  // open: en, clr
  Data_Path data_path_1 (
    .Write_PC(MIR_q[5]), .MBR_In(Memory_In), .Write_MBR(MIR_q[4]), .Write_OUT(MIR_q[6]), .Write_B(MIR_q[3]),
    .Write_A(MIR_q[2]), .PC_Out(Memory_Address), .OUT_Out(Output), .Switch_Input(Input),
    .B_Bus_Select(MIR_q[1:0]), .F(MIR_q[9:7]), .Clock(Clock),
    .MBR_Out({data_path_1_mbr_out_2, data_path_1_mbr_out}));

  // Notes on the sheet:
  //   Virtual MPC
  //   contents of rom_1 (hex, n*v repeats v):
  //   1254 0 2254 0 254
endmodule
